# Fritzing sketch Mobicool8266 (saved by Fritzing 0.9.10b)
circuit board: 9.29217cm x 5.16772cm
breadboards: 1

parts:
  WeMos_D1_Mini1 = WeMos D1 Mini
  U2 = Sharp PC817 [package=THT]
  U3 = Sharp PC817 [package=THT]
  U4 = Sharp PC817 [package=THT]
  R3 = Resistor [tolerance=±5% resistance=4.7k power=0.25 package=THT]
  R1 = Resistor [tolerance=±5% resistance=4.7k power=0.25 package=THT]
  R4 = Resistor [tolerance=±5% resistance=4.7k power=0.25 package=THT]
  R2 = Resistor [tolerance=±5% resistance=4.7k power=0.25 package=THT]
  NTC_Voltage = female pin header, 1 pin [form="♀ (female)"]
  3v3 = female pin header, 1 pin [form="♀ (female)"]
  GND = female pin header, 1 pin [form="♀ (female)"]
  J4 = female pin header, 1 pin [form="♀ (female)"]
  J5 = female pin header, 1 pin [form="♀ (female)"]
  J6 = female pin header, 1 pin [form="♀ (female)"]
  J7 = female pin header, 1 pin [form="♀ (female)"]
  J8 = female pin header, 1 pin [form="♀ (female)"]
  U1 = Sharp PC817 [package=THT]
  R5 = Resistor [tolerance=±5% resistance=4.7k power=0.25 package=THT]
  J9 = female pin header, 4 pins [form="♀ (female)"]

nets:
  N1: WeMos_D1_Mini1.3V3, 3v3.pin1, R5.Pin_0, J9.pin2
  N2: WeMos_D1_Mini1.A0, NTC_Voltage.pin1
  N3: WeMos_D1_Mini1.D1, R5.Pin_1, J9.pin4
  N4: WeMos_D1_Mini1.D2, R3.Pin_1
  N5: WeMos_D1_Mini1.D3, R4.Pin_1
  N6: WeMos_D1_Mini1.D5, J9.pin1
  N7: WeMos_D1_Mini1.D6, R2.Pin_1
  N8: WeMos_D1_Mini1.D7, R1.Pin_1
  GND: WeMos_D1_Mini1.G, U2.Pin_2, U3.Pin_2, U4.Pin_2, GND.pin1, U1.Pin_2, J9.pin3
  N9: U2.Pin_1, R2.Pin_0
  N10: U2.Pin_4, J7.pin1
  N11: U2.Pin_3, U3.Pin_3, U4.Pin_3, J4.pin1, U1.Pin_3
  N12: U3.Pin_1, R3.Pin_0
  N13: U3.Pin_4, J6.pin1
  N14: U4.Pin_1, R4.Pin_0
  N15: U4.Pin_4, J5.pin1
  N16: R1.Pin_0, U1.Pin_1
  N17: J8.pin1, U1.Pin_4
